// Logisim project 4-BIT CPU.circ as structural Verilog: 4 circuits, main circuit Main
module Main (
  input  in_1
);

  wire and_1_out, and_2_out, and_3_out, and_4_out, and_5_out, and_6_out, and_7_out, and_8_out, and_9_out,
       and_10_out, and_11_out, and_12_out, and_13_out, and_14_out, and_15_out, and_16_out, Clock_out,
       multiplexer_2_out, multiplexer_3_out, multiplexer_4_out, multiplexer_5_out, nor_1_out, not_1_out,
       not_2_out, not_3_out, not_4_out, not_5_out, or_1_out, or_2_out, or_3_out, or_4_out, or_5_out,
       or_6_out, or_7_out, or_8_out, Output_register_q, xor_1_out, xor_2_out, xor_3_out, xor_4_out,
       xor_9_out, xor_10_out, xor_11_out, xor_12_out;
  wire [3:0] counter_1_q, multiplexer_1_out, register_1_q, Register_A_out_7, Register_B_out_7, xor_5_out,
       xor_13_out;
  wire [7:0] rom_1_data;

  Counter #(.width(4), .max('hf)) counter_1 (.Q(counter_1_q), .clk(Clock_out));  // open: load, D, count, carry, clr
  Multiplexer #(.width(4), .disabled(0), .enable("false")) multiplexer_1 (
    .in0(counter_1_q), .in1(xor_5_out), .out(multiplexer_1_out), .sel(Output_register_q));
  xor xor_1 (xor_1_out, 1'b1, counter_1_q[0]);
  xor xor_2 (xor_2_out, in_1, counter_1_q[1]);
  xor xor_3 (xor_3_out, in_1, counter_1_q[2]);
  xor xor_4 (xor_4_out, in_1, counter_1_q[3]);
  xor xor_5 (xor_5_out[0], xor_1_out, in_1);
  and and_1 (and_1_out, counter_1_q[0], 1'b1);
  or or_1 (or_1_out, and_1_out, and_2_out);
  and and_2 (and_2_out, xor_1_out, in_1);
  xor xor_6 (xor_5_out[1], xor_2_out, or_1_out);
  and and_3 (and_3_out, counter_1_q[1], in_1);
  and and_4 (and_4_out, xor_2_out, or_1_out);
  xor xor_7 (xor_5_out[2], xor_3_out, or_4_out);
  and and_5 (and_5_out, counter_1_q[2], in_1);
  or or_2 (or_2_out, and_5_out, and_6_out);
  and and_6 (and_6_out, xor_3_out, or_4_out);
  xor xor_8 (xor_5_out[3], xor_4_out, or_2_out);
  and and_7 (and_7_out, counter_1_q[3], in_1);
  or or_3 (or_3_out, and_7_out, and_8_out);
  and and_8 (and_8_out, xor_4_out, or_2_out);
  ROM_part #(.addrWidth(4)) rom_1 (.addr(multiplexer_1_out), .data(rom_1_data));  // open: sel
  or or_4 (or_4_out, and_3_out, and_4_out);
  LED Carry (.in(or_3_out));
  Register Register_A (
    ._3(rom_1_data[0]), ._2(rom_1_data[1]), ._1(rom_1_data[2]), ._0(rom_1_data[3]), .Clock(not_1_out),
    .Enable(rom_1_data[4]), .out_7(Register_A_out_7[0]), .out_8(Register_A_out_7[1]),
    .out_9(Register_A_out_7[2]), .out_10(Register_A_out_7[3]));
  Register Register_B (
    ._3(rom_1_data[0]), ._2(rom_1_data[1]), ._1(rom_1_data[2]), ._0(rom_1_data[3]), .Clock(not_1_out),
    .Enable(rom_1_data[6]), .out_7(Register_B_out_7[0]), .out_8(Register_B_out_7[1]),
    .out_9(Register_B_out_7[2]), .out_10(Register_B_out_7[3]));
  not not_1 (not_1_out, Clock_out);
  Clock Clock (.out(Clock_out));
  Hex_Digit_Display hex_digit_display_1 (.value(Register_A_out_7));  // open: dp
  Hex_Digit_Display hex_digit_display_2 (.value(Register_B_out_7));  // open: dp
  Multiplexer #(.enable("false")) multiplexer_2 (
    .in0(Register_B_out_7[0]), .in1(not_2_out), .out(multiplexer_2_out), .sel(rom_1_data[7]));
  not not_2 (not_2_out, Register_B_out_7[0]);
  Multiplexer #(.disabled(0), .enable("false")) multiplexer_3 (
    .in0(Register_B_out_7[1]), .in1(not_3_out), .out(multiplexer_3_out), .sel(rom_1_data[7]));
  not not_3 (not_3_out, Register_B_out_7[1]);
  Multiplexer #(.disabled(0), .enable("false")) multiplexer_4 (
    .in0(Register_B_out_7[2]), .in1(not_4_out), .out(multiplexer_4_out), .sel(rom_1_data[7]));
  not not_4 (not_4_out, Register_B_out_7[2]);
  Multiplexer #(.disabled(0), .enable("false")) multiplexer_5 (
    .in0(Register_B_out_7[3]), .in1(not_5_out), .out(multiplexer_5_out), .sel(rom_1_data[7]));
  not not_5 (not_5_out, Register_B_out_7[3]);
  xor xor_9 (xor_9_out, Register_A_out_7[0], multiplexer_2_out);
  xor xor_10 (xor_10_out, Register_A_out_7[1], multiplexer_3_out);
  xor xor_11 (xor_11_out, Register_A_out_7[2], multiplexer_4_out);
  xor xor_12 (xor_12_out, Register_A_out_7[3], multiplexer_5_out);
  xor xor_13 (xor_13_out[0], xor_9_out, rom_1_data[7]);
  and and_9 (and_9_out, multiplexer_2_out, Register_A_out_7[0]);
  and and_10 (and_10_out, xor_9_out, rom_1_data[7]);
  xor xor_14 (xor_13_out[1], xor_10_out, or_5_out);
  and and_11 (and_11_out, multiplexer_3_out, Register_A_out_7[1]);
  and and_12 (and_12_out, xor_10_out, or_5_out);
  xor xor_15 (xor_13_out[2], xor_11_out, or_6_out);
  and and_13 (and_13_out, multiplexer_4_out, Register_A_out_7[2]);
  and and_14 (and_14_out, xor_11_out, or_6_out);
  xor xor_16 (xor_13_out[3], xor_12_out, or_7_out);
  and and_15 (and_15_out, multiplexer_5_out, Register_A_out_7[3]);
  and and_16 (and_16_out, xor_12_out, or_7_out);
  or or_5 (or_5_out, and_9_out, and_10_out);
  or or_6 (or_6_out, and_11_out, and_12_out);
  or or_7 (or_7_out, and_13_out, and_14_out);
  or or_8 (or_8_out, and_15_out, and_16_out);
  LED Carry_2 (.in(or_8_out));
  LED Negative (.in(xor_13_out[3]));
  Register_part #(.width(1)) Output_register (.D(nor_1_out), .Q(Output_register_q), .clk(Clock_out));  // open: en, clr
  LED Zero (.in(nor_1_out));
  nor nor_1 (nor_1_out, xor_13_out[0], xor_13_out[1], xor_13_out[3], xor_13_out[3]);
  Hex_Digit_Display hex_digit_display_3 (.value(register_1_q));  // open: dp
  Register_part #(.width(4)) register_1 (
    .D(xor_13_out), .en(rom_1_data[5]), .Q(register_1_q), .clk(Clock_out));  // open: clr

  // Notes on the sheet:
  //   Counter
  //   ROM
  //   4 BIT CPU
  //   Hex display A
  //   Hex display B
  //   Full Adder
endmodule

module ROM (
  output _0,
  output _1,
  output _2,
  output _3,
  output reg_b_e,
  output output_reg,
  output reg_a_e,
  output mode,
  output out_9
);

  wire [3:0] counter_1_q;

  Counter #(.width(4), .max('hf)) counter_1 (.Q(counter_1_q), .clk(out_9));  // open: load, D, count, carry, clr
  ROM_part #(.addrWidth(4)) rom_1 (
    .addr(counter_1_q), .data({mode, reg_a_e, output_reg, reg_b_e, _3, _2, _1, _0}));  // open: sel

  // Notes on the sheet:
  //   contents of rom_1 (hex, n*v repeats v):
  //   0 42 13
endmodule

module Register (
  input  _3,
  input  _2,
  input  _1,
  input  _0,
  input  Clock,
  input  Enable,
  output out_7,
  output out_8,
  output out_9,
  output out_10
);

  Register_part #(.width(1)) register_1 (.D(_3), .en(Enable), .Q(out_7), .clk(Clock));  // open: clr
  Register_part #(.width(1)) register_2 (.D(_2), .en(Enable), .Q(out_8), .clk(Clock));  // open: clr
  Register_part #(.width(1)) register_3 (.D(_1), .en(Enable), .Q(out_9), .clk(Clock));  // open: clr
  Register_part #(.width(1)) register_4 (.D(_0), .en(Enable), .Q(out_10), .clk(Clock));  // open: clr
endmodule

module last (
);

  wire undriven_3;
  wire [3:0] multiplexer_1_out, undriven, undriven_2;

  Multiplexer #(.width(4), .disabled(0), .enable("false")) multiplexer_1 (
    .in0(undriven_2), .in1(undriven), .out(multiplexer_1_out), .sel(undriven_3));
endmodule
